# Fritzing sketch REMS Sketch (saved by Fritzing 0.9.9b)
stripboards: 4

parts:
  J2 = Camdenboss CTB0158-9 [part_number=CTB0158-9 package=THT]
  J3 = ATX24 Pin Power Supply Connector [package=atx24_right_angle]
  F1 = FUSE [package=fuse_5mm]
  F2 = FUSE [package=fuse_5mm]
  F3 = FUSE [package=fuse_5mm]
  F4 = FUSE [package=fuse_5mm]
  LED1 = smd LED [color="Red (633nm)" package="0805 [SMD]"]
  R1 = Resistor [tolerance=±5% power=0.25 resistance=220 package=THT]
  U1 = SWITCH_SPDT [package=kps-1290]
  S1 = Momentary Switch [package=tactile-pth]
  S2 = Square Pushbutton
  Mod1 = Voltage Sensor 25V
  Part2 = ACS712 Current Sensor 5A 20A 30A
  Mod2 = Voltage Sensor 25V
  Mod3 = Voltage Sensor 25V
  Part3 = ACS712 Current Sensor 5A 20A 30A
  Part4 = ACS712 Current Sensor 5A 20A 30A
  R2 = Resistor [tolerance=±5% resistance=1k package="2010 [SMD]"]
  R4 = Trimmer Potentiometer [maximum_resistance=10kΩ package=THT]
  LCD1 = LCD screen
  Part5 = Arduino Nano (Rev3.0)
  R5 = Resistor [tolerance=±5% resistance=1k package="2010 [SMD]"]
  Part6 = Gas Sensor Breakout Board  # not connected
  Part7 = BME280 Breakout
  J7 = Camdenboss CTB0158-2 [part_number=CTB0158-2 package=THT]
  J8 = Camdenboss CTB0158-2 [part_number=CTB0158-2 package=THT]
  J9 = Camdenboss CTB0158-2 [part_number=CTB0158-2 package=THT]
  R6 = Resistor [tolerance=±5% resistance=1k package="0402 [SMD]"]
  J11 = Camdenboss CTB0158-3 [part_number=CTB0158-3 package=THT]
  Part8 = Arduino Mega 2560 (Rev3)
  LED4 = RGB LED (com. cathode, rbg) [package="5 mm [THT]"]

nets (from the breadboard view):
  N1: J2.pin1, F1.2
  N2: J2.pin2, J2.pin4, J2.pin6, J2.pin8, J3.GND, R1.Pin_0, U1.S, S2.leg0
  N3: J2.pin3, J3.5V_STDBY
  N4: J2.pin5, F4.2
  N5: J2.pin7, F3.2
  N6: J2.pin9, F2.2
  VCC: J2.terminal_1, Part2.2, Part2.VCC, Part2.OUT, Mod2.VCC, Mod3.VCC, Part3.2, Part3.VCC, Part3.OUT, Part4.1, Part4.VCC, R4.leg2, LCD1.VDD, Part5.A0, R5.Pin_0, J7.pin1, J8.pin1, J9.pin1, J11.pin1, Part8.A2, Part8.A4, Part8.VIN
  N7: J2.terminal_3, Part5.VIN
  N8: J2.terminal_4, Part5.GND, LED4.common_cathode
  N9: J2.terminal_5, Part4.2, Part4.OUT, Part8.A3
  GND: J2.terminal_8, S1.3, S1.4, Mod1.GND, Mod1.-, Part2.GND, Mod2.GND, Mod2.-, Mod3.GND, Mod3.-, Part3.GND, Part4.GND, R2.Pin_1, LCD1.VSS, LCD1.R/W, LCD1.LED-, R5.Pin_1, Part7.GND, J7.pin2, J8.pin2, J9.pin2, R6.Pin_0, Part8.GND
  N10: J2.terminal_9, Part3.1
  N11: J3.3.3V, F1.1
  N12: J3.5V, F4.1, LED1.cathode
  N13: J3.12V, F2.1
  N14: J3.-12V, F3.1
  N15: J3.PS_ON, U1.O, U1.P, S2.leg1
  N16: S1.1, S1.2, Part5.RESET, Part8.D10_PWM, Part8.RESET
  N17: Mod1.VCC, Part2.1
  N18: Mod1.S, Part8.A0
  N19: Mod2.S, Part8.A5
  N20: Mod3.S, Part8.A1
  N21: R2.Pin_0, Part5.D10, Part8.D8_PWM
  N22: R4.leg1, LCD1.E, Part8.D6_PWM
  N23: LCD1.RS, Part8.D7_PWM
  N24: LCD1.DB2, LCD1.DB3, LCD1.DB4, Part8.D5_PWM
  N25: LCD1.DB5, Part8.D4_PWM
  N26: LCD1.DB6, Part8.D3_PWM
  N27: LCD1.DB7, Part8.D2_PWM
  N28: Part5.D2, LED4.red_anode
  N29: Part5.D3, LED4.green_anode
  N30: Part5.D4, LED4.blue_anode
  N31: Part5.D11/MOSI, Part8.D13_PWM
  N32: Part5.D12/MISO, Part8.D11_PWM
  N33: Part5.D13/SCK, Part8.D12_PWM
  3.3V: Part7.3.3V, Part8.3V3
  N34: Part7.SDI/SDA, Part8.SDA
  N35: Part7.SCK/SCL, Part8.D21/SCL, Part8.SCL
  N36: R6.Pin_1, J11.pin3, Part8.D9_PWM

custom parts:
  ACS712 Current Sensor 5A 20A 30A: Remix by Michael Kubina http://www.kubina.info Original by: https://forum.fritzing.org/t/current-sensor-5a-acs712/7694 https://forum.fritzing.org/u/ArtHome ArtHome12@gmail.com
